// Logisim project csc256lab7.circ as structural Verilog: 40 circuits, main circuit main
module main (
  input  sw0,
  input  sw1,
  input  sw2,
  input  sw3,
  output [6:0] out_5
);

  seq0 seq0_1 (.sw0(sw0), .sw1(sw1), .sw2(sw2), .sw3(sw3), .m(out_5[0]));
  seq1 seq1_1 (.sw0(sw0), .sw1(sw1), .sw2(sw2), .sw3(sw3), .m(out_5[1]));
  seq2 seq2_1 (.sw0(sw0), .sw1(sw1), .sw2(sw2), .sw3(sw3), .m(out_5[2]));
  seq3 seq3_1 (.sw0(sw0), .sw1(sw1), .sw2(sw2), .sw3(sw3), .m(out_5[3]));
  seq4 seq4_1 (.sw0(sw0), .sw1(sw1), .sw2(sw2), .sw3(sw3), .m(out_5[4]));
  seq5 seq5_1 (.sw0(sw0), .sw1(sw1), .sw2(sw2), .sw3(sw3), .m(out_5[5]));
  seq6 seq6_1 (.sw0(sw0), .sw1(sw1), .sw2(sw2), .sw3(sw3), .m(out_5[6]));
endmodule

module lab7p11 (
  input  in_1,
  input  in_2,
  input  in_3,
  input  in_4
);

  wire clock_1_out;
  wire [3:0] lab7p13_1_out_4, ram_1_dout;
  wire [4:0] lab7p12_1_out_4;
  wire [6:0] main_1_out_5;

  Clock clock_1 (.out(clock_1_out));
  lab7p12 lab7p12_1 (.reset(in_1), .load(in_2), .clk(clock_1_out), .out_4(lab7p12_1_out_4));
  lab7p13 lab7p13_1 (.reset(in_1), .load(in_2), .clk(clock_1_out), .out_4(lab7p13_1_out_4));
  RAM #(.addrWidth(5), .dataWidth(4)) ram_1 (
    .addr(lab7p12_1_out_4), .we(in_3), .oe(in_4), .clk(clock_1_out), .din(lab7p13_1_out_4), .dout(ram_1_dout));
  main main_1 (
    .sw0(ram_1_dout[0]), .sw1(ram_1_dout[1]), .sw2(ram_1_dout[2]), .sw3(ram_1_dout[3]), .out_5(main_1_out_5));
  _7_Segment_Display u_7_segment_display_1 (
    .g(main_1_out_5[6]), .f(main_1_out_5[5]), .a(main_1_out_5[0]), .b(main_1_out_5[1]), .e(main_1_out_5[4]),
    .d(main_1_out_5[3]), .c(main_1_out_5[2]));  // open: dp
endmodule

module lab7p12 (
  input  reset,
  input  load,
  input  clk,
  output [4:0] out_4
);

  wire [4:0] bit_extender_1_out;

  assign bit_extender_1_out = {{4{1'b0}}, 1'b0};  // Bit_Extender bit_extender_1
  Counter #(.max('h1f), .width(5)) counter_1 (
    .clr(reset), .load(load), .up(1'b1), .clk(clk), .D(bit_extender_1_out), .Q(out_4));  // open: count, carry
endmodule

module lab7p13 (
  input  reset,
  input  load,
  input  clk,
  output [3:0] out_4
);

  wire [3:0] bit_extender_1_out;

  assign bit_extender_1_out = {{3{1'b0}}, 1'b0};  // Bit_Extender bit_extender_1
  Counter #(.max('hf), .width(4)) counter_1 (
    .clr(reset), .load(load), .up(1'b1), .clk(clk), .D(bit_extender_1_out), .Q(out_4));  // open: count, carry
endmodule

module lab4p1 (
  input  D,
  input  Clk,
  output out_3,
  output Q,
  output Qb
);

  wire lab4p11_1_q, not_1_out;

  not not_1 (not_1_out, Clk);
  lab4p11 lab4p11_1 (.D(D), .Clk(Clk), .Q(lab4p11_1_q), .Qb(out_3));
  lab4p11 lab4p11_2 (.D(lab4p11_1_q), .Clk(not_1_out), .Q(Q), .Qb(Qb));
endmodule

module mux2to1 (
  input  x,
  input  y,
  input  s,
  output m
);

  Multiplexer #(.enable("false")) multiplexer_1 (.in0(x), .in1(y), .out(m), .sel(s));
endmodule

module mux4to1 (
  input  u,
  input  v,
  input  w,
  input  x,
  input  s1,
  input  s0,
  output m
);

  wire multiplexer_1_out, multiplexer_2_out;

  Multiplexer #(.enable("false")) multiplexer_1 (.in0(u), .in1(v), .out(multiplexer_1_out), .sel(s0));
  Multiplexer #(.enable("false")) multiplexer_2 (.in0(w), .in1(x), .out(multiplexer_2_out), .sel(s0));
  Multiplexer #(.enable("false")) multiplexer_3 (.in0(multiplexer_1_out), .in1(multiplexer_2_out), .out(m), .sel(s1));
endmodule

module mapping (
  input  sw0,
  input  sw1,
  input  sw2,
  input  sw3,
  input  sw9,
  input  sw8,
  output LEDR_9
);

  wire multiplexer_1_out, multiplexer_2_out;

  Multiplexer #(.enable("false")) multiplexer_1 (.in0(sw0), .in1(sw1), .out(multiplexer_1_out), .sel(sw8));
  Multiplexer #(.enable("false")) multiplexer_2 (.in0(sw2), .in1(sw3), .out(multiplexer_2_out), .sel(sw8));
  Multiplexer #(.enable("false")) multiplexer_3 (
    .in0(multiplexer_1_out), .in1(multiplexer_2_out), .out(LEDR_9), .sel(sw9));
endmodule

module seq1 (
  input  sw0,
  input  sw1,
  input  sw2,
  input  sw3,
  output m
);

  wire and_1_out, and_2_out, and_3_out, and_4_out, and_5_out, not_1_out, not_2_out, not_3_out, not_4_out;

  not not_1 (not_1_out, sw0);
  not not_2 (not_2_out, sw1);
  not not_3 (not_3_out, sw2);
  not not_4 (not_4_out, sw3);
  and and_1 (and_1_out, not_1_out, not_2_out, not_4_out);
  and and_2 (and_2_out, sw0, sw3, not_2_out);
  and and_3 (and_3_out, not_2_out, not_3_out);
  and and_4 (and_4_out, not_1_out, sw1, not_3_out);
  and and_5 (and_5_out, sw1, not_4_out, sw0);
  or or_1 (m, and_1_out, and_2_out, and_3_out, and_4_out, and_5_out);
endmodule

module seq2 (
  input  sw0,
  input  sw1,
  input  sw2,
  input  sw3,
  output m
);

  wire and_1_out, and_2_out, and_3_out, and_4_out, and_5_out, not_1_out, not_2_out, not_3_out;

  not not_1 (not_1_out, sw1);
  not not_2 (not_2_out, sw2);
  not not_3 (not_3_out, sw3);
  and and_1 (and_1_out, not_1_out, not_3_out);
  and and_2 (and_2_out, not_2_out, sw3);
  and and_3 (and_3_out, not_3_out, sw2);
  and and_4 (and_4_out, sw0, not_1_out);
  and and_5 (and_5_out, sw1, not_3_out, sw0);
  or or_1 (m, and_1_out, and_2_out, and_3_out, and_4_out, and_5_out);
endmodule

module seq3 (
  input  sw0,
  input  sw1,
  input  sw2,
  input  sw3,
  output m
);

  wire and_1_out, and_2_out, and_3_out, and_4_out, and_5_out, and_6_out, not_1_out, not_2_out, not_3_out,
       not_4_out;

  not not_1 (not_1_out, sw0);
  not not_2 (not_2_out, sw1);
  not not_3 (not_3_out, sw2);
  not not_4 (not_4_out, sw3);
  and and_1 (and_1_out, not_1_out, not_2_out, not_3_out);
  and and_2 (and_2_out, sw0, not_2_out, sw2);
  and and_3 (and_3_out, sw1, sw0, not_3_out);
  and and_4 (and_4_out, not_1_out, sw1, sw2);
  and and_5 (and_5_out, not_2_out, sw3, sw2);
  and and_6 (and_6_out, sw1, not_4_out, not_3_out);
  or or_1 (m, and_1_out, and_2_out, and_3_out, and_4_out, and_5_out, and_6_out);
endmodule

module seq4 (
  input  sw0,
  input  sw1,
  input  sw2,
  input  sw3,
  output m
);

  wire and_1_out, and_2_out, and_3_out, and_4_out, not_1_out, not_2_out, not_3_out;

  not not_1 (not_1_out, sw0);
  not not_2 (not_2_out, sw2);
  not not_3 (not_3_out, sw1);
  and and_1 (and_1_out, not_1_out, sw1);
  and and_2 (and_2_out, sw2, sw3);
  and and_3 (and_3_out, sw1, not_2_out, sw3);
  and and_4 (and_4_out, not_1_out, not_3_out, not_2_out);
  or or_1 (m, and_1_out, and_2_out, and_3_out, and_4_out);
endmodule

module seq5 (
  input  sw0,
  input  sw1,
  input  sw2,
  input  sw3,
  output m
);

  wire and_1_out, and_2_out, and_3_out, and_4_out, and_5_out, not_1_out, not_2_out, not_3_out, not_4_out;

  not not_1 (not_1_out, sw0);
  not not_2 (not_2_out, sw1);
  not not_3 (not_3_out, sw2);
  not not_4 (not_4_out, sw3);
  and and_1 (and_1_out, not_1_out, not_2_out);
  and and_2 (and_2_out, sw3, not_3_out);
  and and_3 (and_3_out, sw1, sw3);
  and and_4 (and_4_out, not_1_out, sw1, sw2);
  and and_5 (and_5_out, not_4_out, sw2, not_2_out);
  or or_1 (m, and_1_out, and_2_out, and_3_out, and_4_out, and_5_out);
endmodule

module seq6 (
  input  sw0,
  input  sw1,
  input  sw2,
  input  sw3,
  output m
);

  wire and_1_out, and_2_out, and_3_out, and_4_out, and_5_out, and_6_out, not_1_out, not_2_out, not_3_out,
       not_4_out;

  not not_1 (not_1_out, sw0);
  not not_2 (not_2_out, sw2);
  not not_3 (not_3_out, sw3);
  not not_4 (not_4_out, sw1);
  and and_1 (and_1_out, not_2_out, sw3);
  and and_2 (and_2_out, sw1, sw3);
  and and_3 (and_3_out, not_2_out, sw1);
  and and_4 (and_4_out, sw1, not_1_out);
  and and_5 (and_5_out, not_3_out, sw2, not_4_out);
  and and_6 (and_6_out, not_4_out, sw0, sw3);
  or or_1 (m, and_1_out, and_2_out, and_3_out, and_4_out, and_5_out, and_6_out);
endmodule

module seq0 (
  input  sw0,
  input  sw1,
  input  sw2,
  input  sw3,
  output m
);

  wire and_1_out, and_2_out, and_3_out, and_4_out, and_5_out, and_6_out, not_1_out, not_2_out, not_3_out,
       not_4_out;

  not not_1 (not_1_out, sw0);
  not not_2 (not_2_out, sw2);
  not not_3 (not_3_out, sw3);
  not not_4 (not_4_out, sw1);
  and and_1 (and_1_out, sw0, sw2, not_3_out);
  and and_2 (and_2_out, sw2, sw1);
  and and_3 (and_3_out, sw1, not_3_out);
  and and_4 (and_4_out, not_1_out, sw3);
  and and_5 (and_5_out, not_2_out, not_1_out, not_3_out);
  and and_6 (and_6_out, not_4_out, sw3, not_2_out);
  or or_1 (m, and_1_out, and_2_out, and_3_out, and_4_out, and_5_out, and_6_out);
endmodule

module lab3p1 (
  input  [9:0] sw,
  output s
);

  Multiplexer #(.enable("false"), .select(3)) multiplexer_1 (
    .in0(sw[9]), .in1(sw[8]), .in2(sw[7]), .in3(sw[6]), .in4(sw[5]), .in5(sw[4]), .in6(sw[3]), .out(s),
    .sel(sw[2:0]));  // open: in7
endmodule

module lab3p2 (
  input  a,
  input  b,
  input  c_in,
  output c_out,
  output s
);

  wire and_1_out, and_2_out, xor_1_out;

  or or_1 (c_out, and_1_out, and_2_out);
  and and_1 (and_1_out, a, b);
  and and_2 (and_2_out, xor_1_out, c_in);
  xor xor_1 (xor_1_out, a, b);
  xor xor_2 (s, xor_1_out, c_in);
endmodule

module lab3p22 (
  input  [3:0] B,
  input  [3:0] A,
  input  c_in,
  output c_out,
  output [3:0] S
);

  wire lab3p2_2_c_out, lab3p2_3_c_out, lab3p2_4_c_out;

  lab3p2 lab3p2_1 (.a(A[3]), .b(B[3]), .c_in(lab3p2_2_c_out), .c_out(c_out), .s(S[3]));
  lab3p2 lab3p2_2 (.a(A[2]), .b(B[2]), .c_in(lab3p2_3_c_out), .c_out(lab3p2_2_c_out), .s(S[2]));
  lab3p2 lab3p2_3 (.a(A[1]), .b(B[1]), .c_in(lab3p2_4_c_out), .c_out(lab3p2_3_c_out), .s(S[1]));
  lab3p2 lab3p2_4 (.a(A[0]), .b(B[0]), .c_in(c_in), .c_out(lab3p2_4_c_out), .s(S[0]));
endmodule

module lab3p33 (
  input  c_in,
  input  [3:0] A,
  input  [3:0] B,
  output [7:0] S
);

  wire [3:0] adder_1_out;
  wire [4:4] adder_1_cout;

  Adder #(.width(4)) adder_1 (.a(A), .b(B), .out(adder_1_out), .cin(c_in), .cout(adder_1_cout[4]));
  assign S = {{3{1'b0}}, {adder_1_cout[4], adder_1_out}};  // Bit_Extender bit_extender_1
endmodule

module lab3p31 (
  input  [3:0] A,
  output [7:0] s
);

  wire [3:0] lab3p22_1_s;
  wire [4:4] lab3p22_1_c_out;

  lab3p22 lab3p22_1 (.B(4'b0000), .A(A), .c_in(1'b1), .c_out(lab3p22_1_c_out[4]), .S(lab3p22_1_s));
  assign s = {{3{1'b0}}, {lab3p22_1_c_out[4], lab3p22_1_s}};  // Bit_Extender bit_extender_1
endmodule

module lab3p34 (
  input  [3:0] A,
  input  [3:0] B,
  output [7:0] S
);

  wire or_1_out;

  or or_1 (or_1_out, A[0], A[1], A[2], A[3], B[0], B[1], B[2], B[3]);
  assign S = {{7{1'b0}}, or_1_out};  // Bit_Extender bit_extender_1
endmodule

module lab3p32 (
  input  [3:0] A,
  input  [3:0] B,
  output [7:0] S
);

  or or_1 (S[4], A[0], B[0]);
  or or_2 (S[5], A[1], B[1]);
  or or_3 (S[6], A[2], B[2]);
  or or_4 (S[7], A[3], B[3]);
  xor xor_1 (S[0], A[0], B[0]);
  xor xor_2 (S[1], A[1], B[1]);
  xor xor_3 (S[2], A[2], B[2]);
  xor xor_4 (S[3], A[3], B[3]);
endmodule

module lab3p35 (
  input  [3:0] A,
  input  [3:0] B,
  output [7:0] S
);


  assign S = {A, B};
endmodule

module lab3p3 (
  input  [3:0] A,
  input  [2:0] SE,
  input  [3:0] B,
  output [7:0] S
);

  wire [7:0] lab3p23_1_s, lab3p31_1_s, lab3p32_1_s, lab3p33_1_s, lab3p34_1_s, lab3p35_1_s;

  lab3p31 lab3p31_1 (.A(A), .s(lab3p31_1_s));
  lab3p23 lab3p23_1 (.B(B), .A(A), .c_in(1'b0), .S(lab3p23_1_s));
  lab3p33 lab3p33_1 (.c_in(1'b0), .A(A), .B(B), .S(lab3p33_1_s));
  lab3p32 lab3p32_1 (.A(A), .B(B), .S(lab3p32_1_s));
  lab3p34 lab3p34_1 (.A(A), .B(B), .S(lab3p34_1_s));
  lab3p35 lab3p35_1 (.A(A), .B(B), .S(lab3p35_1_s));
  Multiplexer #(.enable("false"), .select(3), .width(8)) multiplexer_1 (
    .in0(lab3p31_1_s), .in1(lab3p23_1_s), .in2(lab3p33_1_s), .in3(lab3p32_1_s), .in4(lab3p34_1_s),
    .in5(lab3p35_1_s), .out(S), .sel(SE));  // open: in6, in7
endmodule

module lab3p23 (
  input  [3:0] B,
  input  [3:0] A,
  input  c_in,
  output [7:0] S
);

  wire [3:0] lab3p22_1_s;
  wire [4:4] lab3p22_1_c_out;

  lab3p22 lab3p22_1 (.B(B), .A(A), .c_in(c_in), .c_out(lab3p22_1_c_out[4]), .S(lab3p22_1_s));
  assign S = {{3{1'b0}}, {lab3p22_1_c_out[4], lab3p22_1_s}};  // Bit_Extender bit_extender_1
endmodule

module lab3p39 (
  input  [3:0] in_1,
  input  [2:0] in_2,
  input  [3:0] in_3
);

  wire [7:0] lab3p3_1_s;

  lab3p3 lab3p3_1 (.A(in_1), .SE(in_2), .B(in_3), .S(lab3p3_1_s));
  LED led_1 (.in(lab3p3_1_s[0]));
  LED led_2 (.in(lab3p3_1_s[1]));
  LED led_3 (.in(lab3p3_1_s[2]));
  LED led_4 (.in(lab3p3_1_s[3]));
  LED led_5 (.in(lab3p3_1_s[4]));
  LED led_6 (.in(lab3p3_1_s[5]));
  LED led_7 (.in(lab3p3_1_s[6]));
  LED led_8 (.in(lab3p3_1_s[7]));
endmodule

module lab3p310 (
  input  [3:0] A,
  input  [2:0] SE,
  input  [3:0] B
);

  wire [6:0] main_1_out_5, main_2_out_5;
  wire [7:0] lab3p3_1_s;

  lab3p3 lab3p3_1 (.A(A), .SE(SE), .B(B), .S(lab3p3_1_s));
  main main_1 (
    .sw0(lab3p3_1_s[0]), .sw1(lab3p3_1_s[1]), .sw2(lab3p3_1_s[2]), .sw3(lab3p3_1_s[3]), .out_5(main_1_out_5));
  main main_2 (
    .sw0(lab3p3_1_s[4]), .sw1(lab3p3_1_s[5]), .sw2(lab3p3_1_s[6]), .sw3(lab3p3_1_s[7]), .out_5(main_2_out_5));
  _7_Segment_Display u_7_segment_display_1 (
    .g(main_1_out_5[6]), .f(main_1_out_5[5]), .a(main_1_out_5[0]), .b(main_1_out_5[1]), .e(main_1_out_5[4]),
    .d(main_1_out_5[3]), .c(main_1_out_5[2]));  // open: dp
  _7_Segment_Display u_7_segment_display_2 (
    .g(main_2_out_5[6]), .f(main_2_out_5[5]), .a(main_2_out_5[0]), .b(main_2_out_5[1]), .e(main_2_out_5[4]),
    .d(main_2_out_5[3]), .c(main_2_out_5[2]));  // open: dp
endmodule

module lab3p311 (
  input  [3:0] A,
  input  [3:0] B
);

  wire [6:0] main_1_out_5, main_2_out_5;

  main main_1 (.sw0(A[0]), .sw1(A[1]), .sw2(A[2]), .sw3(A[3]), .out_5(main_1_out_5));
  main main_2 (.sw0(B[0]), .sw1(B[1]), .sw2(B[2]), .sw3(B[3]), .out_5(main_2_out_5));
  _7_Segment_Display u_7_segment_display_1 (
    .g(main_2_out_5[6]), .f(main_2_out_5[5]), .a(main_2_out_5[0]), .b(main_2_out_5[1]), .e(main_2_out_5[4]),
    .d(main_2_out_5[3]), .c(main_2_out_5[2]));  // open: dp
  _7_Segment_Display u_7_segment_display_2 (
    .g(main_1_out_5[6]), .f(main_1_out_5[5]), .a(main_1_out_5[0]), .b(main_1_out_5[1]), .e(main_1_out_5[4]),
    .d(main_1_out_5[3]), .c(main_1_out_5[2]));  // open: dp
endmodule

module lab4p11 (
  input  D,
  input  Clk,
  output Q,
  output Qb
);

  wire nand_1_out, nand_2_out, not_1_out;

  not not_1 (not_1_out, D);
  nand nand_1 (nand_1_out, D, Clk);
  nand nand_2 (nand_2_out, Clk, not_1_out);
  nand nand_3 (Q, nand_1_out, Qb);
  nand nand_4 (Qb, Q, nand_2_out);
endmodule

module lab4p2 (
  input  [3:0] A,
  input  Clk,
  input  [2:0] c_in,
  input  R,
  output [7:0] Q
);

  wire [7:0] lab3p23_1_s, lab3p31_1_s, lab3p32_1_s, lab3p33_1_s, lab3p34_1_s, lab4p25_1_out_3,
       lab4p26_1_out_3, lab4p27_1_out_3, multiplexer_1_out;

  lab3p31 lab3p31_1 (.A(A), .s(lab3p31_1_s));
  lab3p23 lab3p23_1 (.B(Q[3:0]), .A(A), .c_in(1'b0), .S(lab3p23_1_s));
  lab3p33 lab3p33_1 (.c_in(1'b0), .A(A), .B(Q[3:0]), .S(lab3p33_1_s));
  lab3p32 lab3p32_1 (.A(A), .B(Q[3:0]), .S(lab3p32_1_s));
  lab3p34 lab3p34_1 (.A(A), .B(Q[3:0]), .S(lab3p34_1_s));
  lab4p25 lab4p25_1 (.B(Q[3:0]), .A(A), .out_3(lab4p25_1_out_3));
  lab4p26 lab4p26_1 (.B(Q[3:0]), .A(A), .out_3(lab4p26_1_out_3));
  lab4p27 lab4p27_1 (.A(A), .B(Q[3:0]), .out_3(lab4p27_1_out_3));
  Multiplexer #(.enable("false"), .select(3), .width(8)) multiplexer_1 (
    .in0(lab3p31_1_s), .in1(lab3p23_1_s), .in2(lab3p33_1_s), .in3(lab3p32_1_s), .in4(lab3p34_1_s),
    .in5(lab4p25_1_out_3), .in6(lab4p26_1_out_3), .in7(lab4p27_1_out_3), .out(multiplexer_1_out), .sel(c_in));
  Register register_1 (.D(multiplexer_1_out), .en(1'b1), .clk(Clk), .Q(Q), .clr(R));
endmodule

module lab4p25 (
  input  [3:0] B,
  input  [3:0] A,
  output [7:0] out_3
);

  wire [7:0] bit_extender_1_out;

  assign bit_extender_1_out = {{4{1'b0}}, B};  // Bit_Extender bit_extender_1
  Shifter shifter_1 (.in(bit_extender_1_out), .\dist (A[2:0]), .out(out_3));
endmodule

module lab4p26 (
  input  [3:0] B,
  input  [3:0] A,
  output [7:0] out_3
);

  wire [7:0] bit_extender_1_out;

  assign bit_extender_1_out = {{4{1'b0}}, B};  // Bit_Extender bit_extender_1
  Shifter #(.shift("lr")) shifter_1 (.in(bit_extender_1_out), .\dist (A[2:0]), .out(out_3));
endmodule

module lab4p27 (
  input  [3:0] A,
  input  [3:0] B,
  output [7:0] out_3
);

  wire [7:0] bit_extender_1_out, bit_extender_2_out;

  assign bit_extender_1_out = {{4{1'b0}}, A};  // Bit_Extender bit_extender_1
  assign bit_extender_2_out = {{4{B[3]}}, B};  // Bit_Extender bit_extender_2
  Multiplier multiplier_1 (.a(bit_extender_1_out), .b(bit_extender_2_out), .cout(out_3));  // open: out, cin
endmodule

module lab4p29 (
  input  [3:0] A,
  input  [2:0] in_2,
  input  Clk
);

  wire [6:0] main_1_out_5, main_2_out_5;
  wire [7:0] lab4p2_1_q;

  lab4p2 lab4p2_1 (.A(A), .Clk(Clk), .c_in(in_2), .Q(lab4p2_1_q));  // open: R
  main main_1 (
    .sw0(lab4p2_1_q[0]), .sw1(lab4p2_1_q[1]), .sw2(lab4p2_1_q[2]), .sw3(lab4p2_1_q[3]), .out_5(main_1_out_5));
  main main_2 (
    .sw0(lab4p2_1_q[4]), .sw1(lab4p2_1_q[5]), .sw2(lab4p2_1_q[6]), .sw3(lab4p2_1_q[7]), .out_5(main_2_out_5));
  _7_Segment_Display u_7_segment_display_1 (
    .g(main_1_out_5[6]), .f(main_1_out_5[5]), .a(main_1_out_5[0]), .b(main_1_out_5[1]), .e(main_1_out_5[4]),
    .d(main_1_out_5[3]), .c(main_1_out_5[2]));  // open: dp
  _7_Segment_Display u_7_segment_display_2 (
    .g(main_2_out_5[6]), .f(main_2_out_5[5]), .a(main_2_out_5[0]), .b(main_2_out_5[1]), .e(main_2_out_5[4]),
    .d(main_2_out_5[3]), .c(main_2_out_5[2]));  // open: dp
endmodule

module lab4p31 (
  input  load_val,
  input  c_in,
  input  shift,
  input  load_n,
  input  Clk,
  input  reset,
  output c_out
);

  wire multiplexer_1_out, multiplexer_2_out;

  Multiplexer #(.enable("false")) multiplexer_1 (.in0(c_out), .in1(c_in), .out(multiplexer_1_out), .sel(shift));
  D_Flip_Flop d_ff_1 (.D(multiplexer_2_out), .clk(Clk), .Q(c_out), .reset(reset));  // open: Qn, preset
  Multiplexer #(.enable("false")) multiplexer_2 (
    .in0(load_val), .in1(multiplexer_1_out), .out(multiplexer_2_out), .sel(load_n));
endmodule

module lab4p21 (
  input  [3:0] A,
  input  [2:0] c_in,
  output [7:0] Q
);

  wire [7:0] lab3p23_1_s, lab3p31_1_s, lab3p32_1_s, lab3p33_1_s, lab3p34_1_s, lab4p25_1_out_3,
       lab4p26_1_out_3, lab4p27_1_out_3;

  lab3p31 lab3p31_1 (.A(A), .s(lab3p31_1_s));
  lab3p23 lab3p23_1 (.B(Q[3:0]), .A(A), .c_in(1'b0), .S(lab3p23_1_s));
  lab3p33 lab3p33_1 (.c_in(1'b0), .A(A), .B(Q[3:0]), .S(lab3p33_1_s));
  lab3p32 lab3p32_1 (.A(A), .B(Q[3:0]), .S(lab3p32_1_s));
  lab3p34 lab3p34_1 (.A(A), .B(Q[3:0]), .S(lab3p34_1_s));
  lab4p25 lab4p25_1 (.B(Q[3:0]), .A(A), .out_3(lab4p25_1_out_3));
  lab4p26 lab4p26_1 (.B(Q[3:0]), .A(A), .out_3(lab4p26_1_out_3));
  lab4p27 lab4p27_1 (.A(A), .B(Q[3:0]), .out_3(lab4p27_1_out_3));
  Multiplexer #(.enable("false"), .select(3), .width(8)) multiplexer_1 (
    .in0(lab3p31_1_s), .in1(lab3p23_1_s), .in2(lab3p33_1_s), .in3(lab3p32_1_s), .in4(lab3p34_1_s),
    .in5(lab4p25_1_out_3), .in6(lab4p26_1_out_3), .in7(lab4p27_1_out_3), .out(Q), .sel(c_in));
endmodule

module lab4p32 (
  input  [7:0] LoadVal,
  input  load_n,
  input  Clk,
  input  [7:0] reset,
  input  shiftright,
  input  ASR,
  output [7:0] out_7
);

  wire and_1_out, multiplexer_1_out;

  Multiplexer #(.enable("false")) multiplexer_1 (
    .in0(1'b0), .in1(LoadVal[7]), .out(multiplexer_1_out), .sel(and_1_out));
  and and_1 (and_1_out, shiftright, ASR);
  lab4p31 lab4p31_1 (
    .load_val(LoadVal[0]), .c_in(out_7[1]), .shift(shiftright), .load_n(load_n), .Clk(Clk), .reset(reset[0]),
    .c_out(out_7[0]));
  lab4p31 lab4p31_2 (
    .load_val(LoadVal[1]), .c_in(out_7[2]), .shift(shiftright), .load_n(load_n), .Clk(Clk), .reset(reset[1]),
    .c_out(out_7[1]));
  lab4p31 lab4p31_3 (
    .load_val(LoadVal[2]), .c_in(out_7[3]), .shift(shiftright), .load_n(load_n), .Clk(Clk), .reset(reset[2]),
    .c_out(out_7[2]));
  lab4p31 lab4p31_4 (
    .load_val(LoadVal[3]), .c_in(out_7[4]), .shift(shiftright), .load_n(load_n), .Clk(Clk), .reset(reset[3]),
    .c_out(out_7[3]));
  lab4p31 lab4p31_5 (
    .load_val(LoadVal[4]), .c_in(out_7[5]), .shift(shiftright), .load_n(load_n), .Clk(Clk), .reset(reset[4]),
    .c_out(out_7[4]));
  lab4p31 lab4p31_6 (
    .load_val(LoadVal[5]), .c_in(out_7[6]), .shift(shiftright), .load_n(load_n), .Clk(Clk), .reset(reset[5]),
    .c_out(out_7[5]));
  lab4p31 lab4p31_7 (
    .load_val(LoadVal[6]), .c_in(out_7[7]), .shift(shiftright), .load_n(load_n), .Clk(Clk), .reset(reset[6]),
    .c_out(out_7[6]));
  lab4p31 lab4p31_8 (
    .load_val(LoadVal[7]), .c_in(multiplexer_1_out), .shift(shiftright), .load_n(load_n), .Clk(Clk),
    .reset(reset[7]), .c_out(out_7[7]));
endmodule

module lab7p21 (
  input  [6:0] in_1,
  input  in_2,
  input  in_3,
  input  [6:0] in_4,
  output [6:0] out_5,
  output [6:0] out_6
);

  wire clock_1_out, lab7datapath_1_enable;
  wire [23:0] lab7datapath_1_out_7;

  Clock clock_1 (.out(clock_1_out));
  lab7datapath lab7datapath_1 (
    .X_in(in_1), .reset(in_2), .clk(clock_1_out), .en(in_3), .Y_in(in_4), .X(out_5),
    .out_7(lab7datapath_1_out_7), .enable(lab7datapath_1_enable), .Y(out_6));
  // RGB_Video #(.cursor("No Cursor")) rgb_video_1: pin names not known; wires that end beside it: in_2, clock_1_out, lab7datapath_1_enable, out_5, out_6, lab7datapath_1_out_7
endmodule

module lab7datapath (
  input  [6:0] X_in,
  input  reset,
  input  clk,
  input  en,
  input  [6:0] Y_in,
  output [6:0] X,
  output [23:0] out_7,
  output enable,
  output [6:0] Y
);

  wire [6:0] lab7fsm_1_x_in, lab7fsm_1_y_in;

  lab7fsm lab7fsm_1 (
    .reset(reset), .in_2(clk), .enable(en), .x_in(lab7fsm_1_x_in), .y_in(lab7fsm_1_y_in), .out_6(enable));
  Adder #(.width(7)) adder_1 (.a(X_in), .b(lab7fsm_1_x_in), .out(X));  // open: cin, cout
  Adder #(.width(7)) adder_2 (.a(Y_in), .b(lab7fsm_1_y_in), .out(Y));  // open: cin, cout
  assign out_7[7:0] = {{7{1'b0}}, 1'b0};  // Bit_Extender bit_extender_1
  assign out_7[15:8] = {{7{1'b1}}, 1'b1};  // Bit_Extender bit_extender_2
  assign out_7[23:16] = {{7{1'b0}}, 1'b0};  // Bit_Extender bit_extender_3
endmodule

module lab7fsm (
  input  reset,
  input  in_2,
  input  enable,
  output [6:0] x_in,
  output [6:0] y_in,
  output out_6
);

  wire and_1_out, and_2_out, and_3_out, not_1_out;
  wire [3:0] bit_extender_1_out, counter_1_q, counter_2_q;

  assign bit_extender_1_out = {{3{1'b0}}, 1'b0};  // Bit_Extender bit_extender_1
  Counter #(.max('hf), .width(4)) counter_1 (
    .clr(reset), .load(1'b0), .up(1'b1), .clk(in_2), .D(bit_extender_1_out), .Q(counter_1_q));  // open: count, carry
  Counter #(.max('hf), .width(4)) counter_2 (
    .clr(reset), .load(1'b0), .up(1'b1), .clk(and_1_out), .D(bit_extender_1_out), .Q(counter_2_q));  // open: count, carry
  and and_1 (and_1_out, counter_1_q[0], counter_1_q[1], counter_1_q[2], counter_1_q[3]);
  assign y_in = {{3{1'b0}}, counter_2_q};  // Bit_Extender bit_extender_2
  assign x_in = {{3{1'b0}}, counter_1_q};  // Bit_Extender bit_extender_3
  and and_2 (and_2_out, counter_2_q[0], counter_2_q[1], counter_2_q[2], counter_2_q[3]);
  and and_3 (and_3_out, and_1_out, and_2_out);
  not not_1 (not_1_out, and_3_out);
  and and_4 (out_6, not_1_out, enable);
endmodule
