// Logisim project lab2.circ as structural Verilog: 11 circuits, main circuit main
module main (
  input  sw0,
  input  sw1,
  input  sw2,
  input  sw3
);

  wire seq0_1_m, seq1_1_m, seq2_1_m, seq3_1_m, seq4_1_m, seq5_1_m, seq6_1_m;

  seq0 seq0_1 (.sw0(sw0), .sw1(sw1), .sw2(sw2), .sw3(sw3), .m(seq0_1_m));
  seq1 seq1_1 (.sw0(sw0), .sw1(sw1), .sw2(sw2), .sw3(sw3), .m(seq1_1_m));
  seq2 seq2_1 (.sw0(sw0), .sw1(sw1), .sw2(sw2), .sw3(sw3), .m(seq2_1_m));
  seq3 seq3_1 (.sw0(sw0), .sw1(sw1), .sw2(sw2), .sw3(sw3), .m(seq3_1_m));
  seq4 seq4_1 (.sw0(sw0), .sw1(sw1), .sw2(sw2), .sw3(sw3), .m(seq4_1_m));
  seq5 seq5_1 (.sw0(sw0), .sw1(sw1), .sw2(sw2), .sw3(sw3), .m(seq5_1_m));
  seq6 seq6_1 (.sw0(sw0), .sw1(sw1), .sw2(sw2), .sw3(sw3), .m(seq6_1_m));
  _7_Segment_Display u_7_segment_display_1 (
    .g(seq6_1_m), .f(seq5_1_m), .a(seq0_1_m), .b(seq1_1_m), .e(seq4_1_m), .d(seq3_1_m), .c(seq2_1_m));  // open: dp
endmodule

module mux2to1 (
  input  x,
  input  y,
  input  s,
  output m
);

  Multiplexer #(.enable("false")) multiplexer_1 (.in0(x), .in1(y), .out(m), .sel(s));
endmodule

module mux4to1 (
  input  u,
  input  v,
  input  w,
  input  x,
  input  s1,
  input  s0,
  output m
);

  wire multiplexer_1_out, multiplexer_2_out;

  Multiplexer #(.enable("false")) multiplexer_1 (.in0(u), .in1(v), .out(multiplexer_1_out), .sel(s0));
  Multiplexer #(.enable("false")) multiplexer_2 (.in0(w), .in1(x), .out(multiplexer_2_out), .sel(s0));
  Multiplexer #(.enable("false")) multiplexer_3 (.in0(multiplexer_1_out), .in1(multiplexer_2_out), .out(m), .sel(s1));
endmodule

module mapping (
  input  sw0,
  input  sw1,
  input  sw2,
  input  sw3,
  input  sw9,
  input  sw8,
  output LEDR_9
);

  wire multiplexer_1_out, multiplexer_2_out;

  Multiplexer #(.enable("false")) multiplexer_1 (.in0(sw0), .in1(sw1), .out(multiplexer_1_out), .sel(sw8));
  Multiplexer #(.enable("false")) multiplexer_2 (.in0(sw2), .in1(sw3), .out(multiplexer_2_out), .sel(sw8));
  Multiplexer #(.enable("false")) multiplexer_3 (
    .in0(multiplexer_1_out), .in1(multiplexer_2_out), .out(LEDR_9), .sel(sw9));
endmodule

module seq1 (
  input  sw0,
  input  sw1,
  input  sw2,
  input  sw3,
  output m
);

  wire and_1_out, and_2_out, and_3_out, and_4_out, and_5_out, not_1_out, not_2_out, not_3_out, not_4_out;

  not not_1 (not_1_out, sw0);
  not not_2 (not_2_out, sw1);
  not not_3 (not_3_out, sw2);
  not not_4 (not_4_out, sw3);
  and and_1 (and_1_out, not_1_out, not_2_out, not_4_out);
  and and_2 (and_2_out, sw0, sw3, not_2_out);
  and and_3 (and_3_out, not_2_out, not_3_out);
  and and_4 (and_4_out, not_1_out, sw1, not_3_out);
  and and_5 (and_5_out, sw1, not_4_out, sw0);
  or or_1 (m, and_1_out, and_2_out, and_3_out, and_4_out, and_5_out);
endmodule

module seq2 (
  input  sw0,
  input  sw1,
  input  sw2,
  input  sw3,
  output m
);

  wire and_1_out, and_2_out, and_3_out, and_4_out, and_5_out, not_1_out, not_2_out, not_3_out;

  not not_1 (not_1_out, sw1);
  not not_2 (not_2_out, sw2);
  not not_3 (not_3_out, sw3);
  and and_1 (and_1_out, not_1_out, not_3_out);
  and and_2 (and_2_out, not_2_out, sw3);
  and and_3 (and_3_out, not_3_out, sw2);
  and and_4 (and_4_out, sw0, not_1_out);
  and and_5 (and_5_out, sw1, not_3_out, sw0);
  or or_1 (m, and_1_out, and_2_out, and_3_out, and_4_out, and_5_out);
endmodule

module seq3 (
  input  sw0,
  input  sw1,
  input  sw2,
  input  sw3,
  output m
);

  wire and_1_out, and_2_out, and_3_out, and_4_out, and_5_out, and_6_out, not_1_out, not_2_out, not_3_out,
       not_4_out;

  not not_1 (not_1_out, sw0);
  not not_2 (not_2_out, sw1);
  not not_3 (not_3_out, sw2);
  not not_4 (not_4_out, sw3);
  and and_1 (and_1_out, not_1_out, not_2_out, not_3_out);
  and and_2 (and_2_out, sw0, not_2_out, sw2);
  and and_3 (and_3_out, sw1, sw0, not_3_out);
  and and_4 (and_4_out, not_1_out, sw1, sw2);
  and and_5 (and_5_out, not_2_out, sw3, sw2);
  and and_6 (and_6_out, sw1, not_4_out, not_3_out);
  or or_1 (m, and_1_out, and_2_out, and_3_out, and_4_out, and_5_out, and_6_out);
endmodule

module seq4 (
  input  sw0,
  input  sw1,
  input  sw2,
  input  sw3,
  output m
);

  wire and_1_out, and_2_out, and_3_out, and_4_out, not_1_out, not_2_out, not_3_out;

  not not_1 (not_1_out, sw0);
  not not_2 (not_2_out, sw2);
  not not_3 (not_3_out, sw1);
  and and_1 (and_1_out, not_1_out, sw1);
  and and_2 (and_2_out, sw2, sw3);
  and and_3 (and_3_out, sw1, not_2_out, sw3);
  and and_4 (and_4_out, not_1_out, not_3_out, not_2_out);
  or or_1 (m, and_1_out, and_2_out, and_3_out, and_4_out);
endmodule

module seq5 (
  input  sw0,
  input  sw1,
  input  sw2,
  input  sw3,
  output m
);

  wire and_1_out, and_2_out, and_3_out, and_4_out, and_5_out, not_1_out, not_2_out, not_3_out, not_4_out;

  not not_1 (not_1_out, sw0);
  not not_2 (not_2_out, sw1);
  not not_3 (not_3_out, sw2);
  not not_4 (not_4_out, sw3);
  and and_1 (and_1_out, not_1_out, not_2_out);
  and and_2 (and_2_out, sw3, not_3_out);
  and and_3 (and_3_out, sw1, sw3);
  and and_4 (and_4_out, not_1_out, sw1, sw2);
  and and_5 (and_5_out, not_4_out, sw2, not_2_out);
  or or_1 (m, and_1_out, and_2_out, and_3_out, and_4_out, and_5_out);
endmodule

module seq6 (
  input  sw0,
  input  sw1,
  input  sw2,
  input  sw3,
  output m
);

  wire and_1_out, and_2_out, and_3_out, and_4_out, and_5_out, and_6_out, not_1_out, not_2_out, not_3_out,
       not_4_out;

  not not_1 (not_1_out, sw0);
  not not_2 (not_2_out, sw2);
  not not_3 (not_3_out, sw3);
  not not_4 (not_4_out, sw1);
  and and_1 (and_1_out, not_2_out, sw3);
  and and_2 (and_2_out, sw1, sw3);
  and and_3 (and_3_out, not_2_out, sw1);
  and and_4 (and_4_out, sw1, not_1_out);
  and and_5 (and_5_out, not_3_out, sw2, not_4_out);
  and and_6 (and_6_out, not_4_out, sw0, sw3);
  or or_1 (m, and_1_out, and_2_out, and_3_out, and_4_out, and_5_out, and_6_out);
endmodule

module seq0 (
  input  sw0,
  input  sw1,
  input  sw2,
  input  sw3,
  output m
);

  wire and_1_out, and_2_out, and_3_out, and_4_out, and_5_out, and_6_out, not_1_out, not_2_out, not_3_out,
       not_4_out;

  not not_1 (not_1_out, sw0);
  not not_2 (not_2_out, sw2);
  not not_3 (not_3_out, sw3);
  not not_4 (not_4_out, sw1);
  and and_1 (and_1_out, sw0, sw2, not_3_out);
  and and_2 (and_2_out, sw2, sw1);
  and and_3 (and_3_out, sw1, not_3_out);
  and and_4 (and_4_out, not_1_out, sw3);
  and and_5 (and_5_out, not_2_out, not_1_out, not_3_out);
  and and_6 (and_6_out, not_4_out, sw3, not_2_out);
  or or_1 (m, and_1_out, and_2_out, and_3_out, and_4_out, and_5_out, and_6_out);
endmodule
